// Logisim project OneBit.circ as structural Verilog: 6 circuits, main circuit main
module main (
  input  in_1,
  input  W,
  input  R,
  input  W_2,
  input  R_2
);

  wire or_1_out, X_write_data, Y_write_data;

  or or_1 (or_1_out, in_1, Y_write_data, X_write_data);
  Register4 X (.Read(R), .Read_Data(or_1_out), .Write(W), .Write_Data(X_write_data));
  Register4 Y (.Read(R_2), .Read_Data(or_1_out), .Write(W_2), .Write_Data(Y_write_data));
endmodule

module Register (
  input  In_Bus,
  input  Clock,
  input  Read,
  input  Write
);

  wire and_1_out, and_2_out, and_3_out, nand_1_out, nand_2_out, nand_3_out, nand_4_out, not_1_out, or_1_out;

  or or_1 (or_1_out, In_Bus, and_1_out);
  and and_1 (and_1_out, nand_4_out, Write);
  and and_2 (and_2_out, Clock, Read);
  and and_3 (and_3_out, Read, or_1_out);
  not not_1 (not_1_out, and_3_out);
  nand nand_1 (nand_1_out, not_1_out, and_2_out);
  nand nand_2 (nand_2_out, and_2_out, and_3_out);
  nand nand_3 (nand_3_out, nand_1_out, nand_4_out);
  nand nand_4 (nand_4_out, nand_3_out, nand_2_out);

  // Notes on the sheet:
  //   Data
endmodule

module Register2 (
  input  In_Bus,
  input  Read,
  input  Write
);

  wire and_1_out, nand_1_out, nand_2_out, nand_3_out, nand_4_out, nand_5_out, not_1_out, or_1_out;

  or or_1 (or_1_out, In_Bus, and_1_out);
  nand nand_1 (nand_1_out, Read, or_1_out);
  and and_1 (and_1_out, nand_5_out, Write);
  not not_1 (not_1_out, nand_1_out);
  nand nand_2 (nand_2_out, nand_1_out, Read);
  nand nand_3 (nand_3_out, Read, not_1_out);
  nand nand_4 (nand_4_out, nand_2_out, nand_5_out);
  nand nand_5 (nand_5_out, nand_4_out, nand_3_out);

  // Notes on the sheet:
  //   Data
endmodule

module Register3 (
  input  In_Bus,
  input  Read,
  input  Write
);

  wire nand_1_out, nand_2_out, nand_3_out, nand_4_out, nand_5_out, nand_6_out, not_1_out, not_2_out, or_1_out;

  or or_1 (or_1_out, In_Bus, not_2_out);
  nand nand_1 (nand_1_out, Read, or_1_out);
  nand nand_2 (nand_2_out, nand_6_out, Write);
  not not_1 (not_1_out, nand_1_out);
  not not_2 (not_2_out, nand_2_out);
  nand nand_3 (nand_3_out, nand_1_out, Read);
  nand nand_4 (nand_4_out, Read, not_1_out);
  nand nand_5 (nand_5_out, nand_3_out, nand_6_out);
  nand nand_6 (nand_6_out, nand_5_out, nand_4_out);

  // Notes on the sheet:
  //   Read Data
  //   Write Data
endmodule

module Register4 (
  input  Read,
  input  Read_Data,
  input  Write,
  output Write_Data
);

  wire nand_1_out, nand_2_out, nand_3_out, nand_4_out, nand_5_out, nand_6_out, not_2_out;

  nand nand_1 (nand_1_out, Read, Read_Data);
  nand nand_2 (nand_2_out, nand_6_out, Write);
  not not_1 (Write_Data, nand_2_out);
  not not_2 (not_2_out, nand_1_out);
  nand nand_3 (nand_3_out, nand_1_out, Read);
  nand nand_4 (nand_4_out, Read, not_2_out);
  nand nand_5 (nand_5_out, nand_3_out, nand_6_out);
  nand nand_6 (nand_6_out, nand_5_out, nand_4_out);
endmodule

module T_Trigger (
  input  in_1,
  input  in_2
);

  wire nand_1_out, nand_2_out, nand_3_out, nand_4_out, pull_resistor_1_node, pull_resistor_2_node,
       pull_resistor_3_node, pull_resistor_4_node, transistor_2_out, transistor_4_out, transistor_6_out,
       transistor_8_out;

  Pull_Resistor #(.pull(1)) pull_resistor_1 (.node(pull_resistor_1_node));
  Transistor #(.\type ("n")) transistor_1 (
    .in(transistor_2_out), .out(pull_resistor_1_node), .gate(pull_resistor_4_node));
  Transistor #(.\type ("n")) transistor_2 (.in(1'b0), .out(transistor_2_out), .gate(in_2));
  Pull_Resistor #(.pull(1)) pull_resistor_2 (.node(pull_resistor_2_node));
  Transistor #(.\type ("n")) transistor_3 (.in(transistor_4_out), .out(pull_resistor_2_node), .gate(in_2));
  Transistor #(.\type ("n")) transistor_4 (.in(1'b0), .out(transistor_4_out), .gate(pull_resistor_3_node));
  nand nand_1 (nand_1_out, nand_4_out, in_1);
  nand nand_2 (nand_2_out, in_1, nand_3_out);
  Pull_Resistor #(.pull(1)) pull_resistor_3 (.node(pull_resistor_3_node));
  Transistor #(.\type ("n")) transistor_5 (
    .in(transistor_6_out), .out(pull_resistor_3_node), .gate(pull_resistor_1_node));
  Transistor #(.\type ("n")) transistor_6 (.in(1'b0), .out(transistor_6_out), .gate(pull_resistor_4_node));
  Pull_Resistor #(.pull(1)) pull_resistor_4 (.node(pull_resistor_4_node));
  Transistor #(.\type ("n")) transistor_7 (
    .in(transistor_8_out), .out(pull_resistor_4_node), .gate(pull_resistor_3_node));
  Transistor #(.\type ("n")) transistor_8 (.in(1'b0), .out(transistor_8_out), .gate(pull_resistor_2_node));
  nand nand_3 (nand_3_out, nand_1_out, nand_4_out);
  nand nand_4 (nand_4_out, nand_3_out, nand_2_out);
endmodule
